# Fritzing sketch Breadboard ADC (saved by Fritzing 1.0.6)
breadboards: 1

parts:
  R1 = Resistor [tolerance=±5% power=0.25W resistance=220 package=THT]
  R3 = Resistor [tolerance=±5% power=0.25W resistance=220 package=THT]
  U1 = LM 358 Dual Op-Amp [package="SO 08 [SMD]"]  # not connected

nets:
  N1: R1.Pin_0, R3.Pin_1
